// Digital circuit FA32.dig as structural Verilog
module FA32 (
  input  [31:0] B,
  input  [31:0] A,
  input  Cin,
  output Cout,
  output [31:0] S
);

  wire fa16_1_cout;

  FA16 fa16_1 (.Cin(Cin), .A(A[15:0]), .B(B[15:0]), .Cout(fa16_1_cout), .S(S[15:0]));
  FA16 fa16_2 (.Cin(fa16_1_cout), .A(A[31:16]), .B(B[31:16]), .Cout(Cout), .S(S[31:16]));
endmodule
