// Digital circuit SLT.dig as structural Verilog
module SLT (
  input  [31:0] rs1,
  input  [31:0] rs2,
  output [31:0] S
);

  wire comparator_1_lt;

  Comparator #(.Bits(32)) comparator_1 (.a(rs1), .b(rs2), .lt(comparator_1_lt));  // open: gt, eq
  BitExtender #(.inputBits(1), .outputBits(32)) bitextender_1 (.in(comparator_1_lt), .out(S));
endmodule
