// Digital circuit Sub32.dig as structural Verilog
module Sub32 (
  input  [31:0] B,
  input  [31:0] A,
  input  Cin,
  output [31:0] S,
  output Cout
);

  wire sub16_1_cout;

  Sub16 sub16_1 (.A(A[15:0]), .B(B[15:0]), .Cin(Cin), .Cout(sub16_1_cout), .S(S[15:0]));
  Sub16 sub16_2 (.A(A[31:16]), .B(B[31:16]), .Cin(sub16_1_cout), .Cout(Cout), .S(S[31:16]));
endmodule
