// Digital circuit ULA.dig as structural Verilog
module ULA (
  input  [31:0] rs2,
  input  [31:0] rs1,
  input  [2:0] FUNC,
  output [31:0] S,
  output ZERO
);

  wire [31:0] and_1_s, fa32_1_s, or_1_s, sll_1_s, slt_1_s, sub32_1_s, xor_1_s;

  FA32 fa32_1 (.B(rs2), .A(rs1), .Cin(1'b0), .S(fa32_1_s));  // open: Cout
  Sub32 sub32_1 (.rs2(rs2), .rs1(rs1), .Cin(1'b1), .S(sub32_1_s));  // open: Cout
  XOR xor_1 (.rs1(rs1), .rs2(rs2), .S(xor_1_s));
  OR or_1 (.rs1(rs1), .rs2(rs2), .S(or_1_s));
  AND and_1 (.rs1(rs1), .rs2(rs2), .S(and_1_s));
  SLL sll_1 (.rs1(rs1), .rs2(rs2), .S(sll_1_s));
  SLT slt_1 (.rs1(rs1), .rs2(rs2), .S(slt_1_s));
  Multiplexer #(.Selector_Bits(3), .Bits(32)) multiplexer_1 (
    .sel(FUNC), .in_0(fa32_1_s), .in_1(sub32_1_s), .in_2(xor_1_s), .in_3(or_1_s), .in_4(and_1_s),
    .in_5(sll_1_s), .in_6(slt_1_s), .in_7({32{1'b0}}), .out(S));
  ZERO zero_1 (.Cin(S), .S(ZERO));
endmodule
